# Fritzing sketch motor_test (saved by Fritzing 0.8.5b)
breadboards: 1

parts:
  BeagleBone1 = BeagleBone Black
  Composants1 = EasyDriver_v44
  M1 = Stepper Motor - Bipolar
  Power_plug1 = Power plug

nets:
  GND: BeagleBone1.no_name_yet#102, Composants1.GND, Power_plug1.GND
  N1: BeagleBone1.no_name_yet#111, Composants1.STEP
  N2: BeagleBone1.no_name_yet#112, Composants1.DIR
  N3: Composants1.V+, Power_plug1.VCC
  N4: Composants1.OUT2A, M1.A
  N5: Composants1.OUT2B, M1.C
  N6: Composants1.OUT1A, M1.B
  N7: Composants1.OUT1B, M1.D

notes:
  solder jumper 3V/5V
  12V

custom parts:
  BeagleBone Black: BeagleBone Black rev. A5B
